# Fritzing sketch exe01_blink (saved by Fritzing 0.9.3b)

parts:
  Componente1 = BlackBoard
  LED1 = smd LED [color="Green (555nm)" package="1206 [SMD]"]

nets:
  N1: Componente1.pin_27, LED1.anode
  N2: Componente1.pin_28, LED1.cathode

custom parts:
  BlackBoard: The Arduino Uno is a microcontroller board based on the ATmega328 (datasheet). It has 14 digital input/output pins (of which 6 can be used as PWM outputs), 6 analog inputs, a 16 MHz ceramic resonator, a USB connection, a power jack, an ICSP header, and a reset button. It contains everything needed to support the microcontroller; simply connect it to a computer with a USB cable or power it with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
