# Fritzing sketch exe04_buzzer (saved by Fritzing 0.9.3b)
breadboards: 1

parts:
  S4 = Pushbutton [package="[THT]"]
  R1 = Resistor [tolerance=±20% resistance=300 package="0603 [SMD]"]
  R2 = Resistor [tolerance=±20% resistance=10k package="0603 [SMD]"]
  LED3 = LED - 3mm [color="Red (633nm)" package="3 mm [THT]"]
  Componente2 = BlackBoard
  S5 = Pushbutton [package="[THT]"]
  S6 = Pushbutton [package="[THT]"]
  R3 = Resistor [tolerance=±20% resistance=10k package="0603 [SMD]"]
  R4 = Resistor [tolerance=±20% resistance=10k package="0603 [SMD]"]
  LED4 = LED - 3mm [color="Yellow (595nm)" package="3 mm [THT]"]
  LED5 = LED - 3mm [color="Green (555nm)" package="3 mm [THT]"]
  R5 = Resistor [tolerance=±20% resistance=300 package="0603 [SMD]"]
  R6 = Resistor [tolerance=±20% resistance=300 package="0603 [SMD]"]
  J1 = Piezo Speaker

nets:
  N1: S4.Pin_1, S4.Pin_2, Componente2.pin_4, S5.Pin_1, S5.Pin_2, S6.Pin_1, S6.Pin_2
  N2: S4.Pin_3, S4.Pin_4, R2.Pin_0, Componente2.pin_20
  N3: R1.Pin_0, LED3.anode
  N4: R1.Pin_1, Componente2.pin_24
  N5: R2.Pin_1, LED3.cathode, Componente2.pin_5, R3.Pin_1, R4.Pin_1, LED4.cathode, LED5.cathode, J1.pin1
  N6: Componente2.pin_16, J1.pin2
  N7: Componente2.pin_18, S6.Pin_3, S6.Pin_4, R3.Pin_0
  N8: Componente2.pin_19, S5.Pin_3, S5.Pin_4, R4.Pin_0
  N9: Componente2.pin_22, R5.Pin_1
  N10: Componente2.pin_26, R6.Pin_1
  N11: LED4.anode, R5.Pin_0
  N12: LED5.anode, R6.Pin_0

custom parts:
  BlackBoard: The Arduino Uno is a microcontroller board based on the ATmega328 (datasheet). It has 14 digital input/output pins (of which 6 can be used as PWM outputs), 6 analog inputs, a 16 MHz ceramic resonator, a USB connection, a power jack, an ICSP header, and a reset button. It contains everything needed to support the microcontroller; simply connect it to a computer with a USB cable or power it with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
