# Fritzing sketch exe02_button_led (saved by Fritzing 0.9.3b)
breadboards: 1

parts:
  S4 = Pushbutton [package="[THT]"]
  R1 = Resistor [tolerance=±20% resistance=300 package="0603 [SMD]"]
  R2 = Resistor [tolerance=±20% resistance=10k package="0603 [SMD]"]  # not connected
  LED3 = LED - 3mm [color="Red (633nm)" package="3 mm [THT]"]
  Componente2 = BlackBoard

nets:
  N1: S4.Pin_1, S4.Pin_2, Componente2.pin_4
  N2: S4.Pin_3, S4.Pin_4, Componente2.pin_16
  N3: R1.Pin_0, Componente2.pin_22
  N4: R1.Pin_1, LED3.anode
  N5: LED3.cathode, Componente2.pin_5

custom parts:
  BlackBoard: The Arduino Uno is a microcontroller board based on the ATmega328 (datasheet). It has 14 digital input/output pins (of which 6 can be used as PWM outputs), 6 analog inputs, a 16 MHz ceramic resonator, a USB connection, a power jack, an ICSP header, and a reset button. It contains everything needed to support the microcontroller; simply connect it to a computer with a USB cable or power it with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
