# Fritzing sketch exe06_temperature_buzzer (saved by Fritzing 0.9.3b)
breadboards: 1

parts:
  Componente2 = BlackBoard
  T1 = LM35 Temperature Sensor [package="TO92 [THT]"]
  J1 = Piezo Speaker

nets:
  N1: Componente2.pin_4, T1.+Vs
  N2: Componente2.pin_5, T1.GND
  N3: Componente2.pin_8, T1.Vout
  N4: Componente2.pin_26, J1.pin2
  N5: Componente2.pin_28, J1.pin1

custom parts:
  BlackBoard: The Arduino Uno is a microcontroller board based on the ATmega328 (datasheet). It has 14 digital input/output pins (of which 6 can be used as PWM outputs), 6 analog inputs, a 16 MHz ceramic resonator, a USB connection, a power jack, an ICSP header, and a reset button. It contains everything needed to support the microcontroller; simply connect it to a computer with a USB cable or power it with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
