# Fritzing sketch exe07_bargraph (saved by Fritzing 0.9.3b)
breadboards: 1

parts:
  Componente2 = BlackBoard
  T1 = LM35 Temperature Sensor [package="TO92 [THT]"]
  J1 = Piezo Speaker
  D1 = LED_BARGRAPH_10 [package=led_bargaph_10]
  R4 = Resistor [tolerance=±20% resistance=300 package="0603 [SMD]"]

nets:
  N1: Componente2.pin_4, T1.+Vs
  N2: Componente2.pin_5, T1.GND
  N3: Componente2.pin_8, T1.Vout
  N4: Componente2.pin_16, D1.J_C
  N5: Componente2.pin_17, D1.I_C
  N6: Componente2.pin_18, D1.H_C
  N7: Componente2.pin_19, D1.G_C
  N8: Componente2.pin_20, D1.F_C
  N9: Componente2.pin_21, D1.E_C
  N10: Componente2.pin_22, D1.D_C
  N11: Componente2.pin_23, D1.C_C
  N12: Componente2.pin_24, D1.B_C
  N13: Componente2.pin_25, D1.A_C
  N14: Componente2.pin_26, J1.pin2
  N15: J1.pin1, R4.Pin_0
  N16: D1.A_A, D1.B_A, D1.C_A, D1.D_A, D1.E_A, D1.F_A, D1.G_A, D1.H_A, D1.I_A, D1.J_A, R4.Pin_1

custom parts:
  BlackBoard: The Arduino Uno is a microcontroller board based on the ATmega328 (datasheet). It has 14 digital input/output pins (of which 6 can be used as PWM outputs), 6 analog inputs, a 16 MHz ceramic resonator, a USB connection, a power jack, an ICSP header, and a reset button. It contains everything needed to support the microcontroller; simply connect it to a computer with a USB cable or power it with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
