# Fritzing sketch exe08_potentiometer (saved by Fritzing 0.9.3b)
breadboards: 1

parts:
  Componente2 = BlackBoard
  R4 = Resistor [tolerance=±20% resistance=300 package="0603 [SMD]"]
  U1 = POT [package=pot_alpha_rv16af-20]
  LED1 = smd LED [color="White (8000K)" package="0805 [SMD]"]

nets:
  N1: Componente2.pin_4, U1.E
  N2: Componente2.pin_5, U1.A, LED1.cathode
  N3: Componente2.pin_8, U1.S
  N4: Componente2.pin_27, R4.Pin_0
  N5: R4.Pin_1, LED1.anode

custom parts:
  BlackBoard: The Arduino Uno is a microcontroller board based on the ATmega328 (datasheet). It has 14 digital input/output pins (of which 6 can be used as PWM outputs), 6 analog inputs, a 16 MHz ceramic resonator, a USB connection, a power jack, an ICSP header, and a reset button. It contains everything needed to support the microcontroller; simply connect it to a computer with a USB cable or power it with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
