# Fritzing sketch exe09_sensor_ldr (saved by Fritzing 0.9.3b)
breadboards: 1

parts:
  Componente2 = BlackBoard
  R4 = Resistor [tolerance=±20% resistance=300 package="0603 [SMD]"]
  LED1 = smd LED [color="White (8000K)" package="0805 [SMD]"]
  R5 = Photocell (LDR) [package=THT]
  R6 = Resistor [tolerance=±20% resistance=10k package="1206 [SMD]"]

nets:
  N1: Componente2.pin_4, R5.pin_0
  N2: Componente2.pin_5, R6.Pin_1
  N3: Componente2.pin_8, R5.pin_1, R6.Pin_0
  N4: Componente2.pin_20, R4.Pin_0
  N5: Componente2.pin_28, LED1.cathode
  N6: R4.Pin_1, LED1.anode

custom parts:
  BlackBoard: The Arduino Uno is a microcontroller board based on the ATmega328 (datasheet). It has 14 digital input/output pins (of which 6 can be used as PWM outputs), 6 analog inputs, a 16 MHz ceramic resonator, a USB connection, a power jack, an ICSP header, and a reset button. It contains everything needed to support the microcontroller; simply connect it to a computer with a USB cable or power it with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
